# Fritzing sketch Diseno_Arduino_Display_Sensor_Rele12V (saved by Fritzing 0.9.1b)
circuit board: 8.2cm x 6.9cm
breadboards: 1

parts:
  Part1 = Arduino Uno (Rev3)
  1K = Resistor [tolerance=±5% resistance=1k package=THT]
  C-B-E = NPN-Transistor [package="TO92 [THT]"]
  J1 = female pin header, 5 pins [form="♀ (female)"]
  Display_16x2 = LCD-16X2 [package=lcd-16x2]
  J4 = female pin header, 8 pins [form="♀ (female)"]  # not connected
  J5 = female pin header, 7 pins [form="♀ (female)"]  # not connected
  220 = Resistor [tolerance=±5% resistance=220 package=THT]
  10k = TRIMPOT [package=trimpot_pth_s3_lock]
  J6 = female pin header, 6 pins [form="♀ (female)"]  # not connected
  Relé = Relay T73
  D1 = Rectifier Diode [part_number=1N4001 package="300 mil [THT]"]
  -_+ = screw terminal, 2 pins
  5v-Data-GND = screw terminal, 3 pins
  4_7k = Resistor [tolerance=±5% resistance=4.7k package=THT]
  Pad9 = Pad [width=4 height=4 connect=center]
  Pad8 = Pad [width=4 height=4 connect=center]  # not connected
  Pad7 = Pad [width=4 height=4 connect=center]  # not connected
  Pad6 = Pad [width=4 height=4 connect=center]  # not connected
  GND--12V = screw terminal, 2 pins
  J7 = female pin header, 16 pins [form="♀ (female)"]  # not connected
  Vin = female pin header, 2 pins [form="♀ (female)"]

nets:
  N1: Part1.D8, Display_16x2.E
  N2: Part1.D9_PWM, Display_16x2.DB4
  N3: Part1.D10_PWM/SS, Display_16x2.DB5
  N4: Part1.D11_PWM/MOSI, Display_16x2.DB6
  N5: Part1.D12/MISO, Display_16x2.DB7
  N6: Part1.D13/SCK, 1K.Pin_1
  N7: Part1.D6_PWM, 5v-Data-GND.pin2, 4_7k.Pin_0
  N8: Part1.D7, Display_16x2.RS
  5V: Part1.5V, Display_16x2.VDD, 220.Pin_0, 10k.CCW
  GND: Part1.GND, C-B-E.E, J1.pin3, Display_16x2.VSS, Display_16x2.R_W, Display_16x2.K, 10k.CW, Relé.COM, 5v-Data-GND.pin1, GND--12V.pin2
  N9: 1K.Pin_0, C-B-E.B
  N10: C-B-E.C, Relé.C1, D1.anode
  N11: J1.pin1, Vin.pin1
  N12: J1.pin4, 5v-Data-GND.pin3, 4_7k.Pin_1
  N13: Display_16x2.VO, 10k.WIPER
  N14: Display_16x2.A, 220.Pin_1
  N15: Relé.C2, D1.cathode
  N16: Relé.NO, -_+.pin2
  N17: -_+.pin1, Pad9.pad, GND--12V.pin1, Vin.pin2

notes:
  Alimentar Arduino con 12V
  Relé y lampara se alimentan con 12v separado (lampara 35 watts)
  Medida PCB
  width 82 mm
  height 69 mm

custom parts:
  Relay T73: An T73 Mini PCB Relay
